# Fritzing sketch Led1 (saved by Fritzing 0.9.3b)
circuit board: 9.29547cm x 7.14407cm

parts:
  LED1 = LED - 5mm [color="Red (633nm)" package="5 mm [THT]"]
  R1 = Resistor [tolerance=±5% resistance=220 package=THT]
  Componente1 = Arduino Uno (Rev3) - ICSP

nets:
  N1: LED1.cathode, R1.Pin_1
  N2: LED1.anode, Componente1.D13/SCK
  N3: R1.Pin_0, Componente1.GND
