# Fritzing sketch proyecto practica 2 (saved by Fritzing 0.9.3b)
circuit board: 11.8205cm x 6.84735cm

parts:
  R1 = Rotary Potentiometer (Small) [maximum_resistance=100kΩ package=THT]
  Practica_2 = Arduino Uno (Rev3)
  LED1 = LED - 5mm [color="Red (633nm)" package="5 mm [THT]"]
  R2 = Resistor [tolerance=±5% resistance=220 package=THT]

nets:
  N1: R1.leg1, Practica_2.D13/SCK
  N2: R1.wiper, LED1.anode
  N3: R1.leg2, Practica_2.GND, R2.Pin_1
  N4: LED1.cathode, R2.Pin_0
