# Fritzing sketch Practica3 (saved by Fritzing 0.9.3b)

parts:
  R2 = Rotary Potentiometer (Small) [maximum_resistance=100kΩ package=THT]
  LED1 = LED - 3mm [color="Red (633nm)" package="3 mm [THT]"]
  Componente1 = Arduino Uno (Rev3)
  R1 = Resistor [tolerance=±5% resistance=220 package="0805 [SMD]"]

nets:
  N1: R2.leg1, Componente1.D13/SCK
  N2: R2.wiper, LED1.anode
  N3: R2.leg2, Componente1.GND, R1.Pin_0

// code stored in the sketch: Untitled2.ino
// the setup routine runs once when you press reset:
void setup() {
  // initialize the digital pin as an output.
  pinMode(13, OUTPUT);
}

// the loop routine runs over and over again forever:
void loop() {
  digitalWrite(13, HIGH);   // turn the LED on (HIGH is the voltage level)
}
